# Fritzing sketch points (saved by Fritzing 0.9.3b)

parts:
  U1 = NodeMCU V1.0
  IC1 = Voltage Regulator [package=to220-igo]
  J1 = Basic Servo
  J2 = Basic Servo
  J3 = Basic Servo

nets:
  GND: U1.GND, IC1.IN, J1.gnd, J2.gnd, J3.gnd
  VCC: U1.Vin, IC1.OUT, J1.vcc, J2.vcc, J3.vcc

notes:
  point 1
  point 2
  point 3

custom parts:
  NodeMCU V1.0: ESP8266 based NodeMCU
