# Fritzing sketch relay (saved by Fritzing 0.9.3b)

parts:
  U1 = NodeMCU V1.0
  IC1 = Voltage Regulator [package=to220-igo]
  Relay_5V1 = Keyes Relay [package=THT]
  Relay_5V2 = Keyes Relay [package=THT]

nets:
  N1: U1.D1, Relay_5V2.signal
  N2: U1.D2, Relay_5V1.signal
  N3: U1.GND, Relay_5V1.ground, Relay_5V2.ground
  N4: U1.Vin, IC1.OUT, Relay_5V1.power, Relay_5V2.power

notes:
  relay 1
  relay 2

custom parts:
  NodeMCU V1.0: ESP8266 based NodeMCU
  Keyes Relay: The Keyes 5V relay module is suitable for SCM development, home appliance control. It uses a 5V~12V TIL control signal which can control DC / AC signal.
