# Fritzing sketch levers (saved by Fritzing 0.9.3b)

parts:
  U1 = NodeMCU V1.0
  U2 = Voltage Regulator - 5V [package="DPak [SMD]"]
  S1 = Toggle Switch [package=THT]
  S2 = Toggle Switch [package=THT]
  S3 = Toggle Switch [package=THT]
  S4 = Toggle Switch [package=THT]
  S5 = Toggle Switch [package=THT]
  S6 = Toggle Switch [package=THT]
  S7 = Toggle Switch [package=THT]
  S8 = Toggle Switch [package=THT]

nets:
  N1: U1.D1, S1.L2
  N2: U1.D2, S2.L2
  N3: U1.D3, S3.L2
  N4: U1.D4, S4.L2
  GND: U1.GND, U2.GND, S1.COM, S2.COM, S3.COM, S4.COM, S5.COM, S6.COM, S7.COM, S8.COM
  N5: U1.D5, S5.L2
  N6: U1.D6, S6.L2
  N7: U1.D7, S7.L2
  N8: U1.TX, S8.L2
  N9: U1.Vin, U2.output_voltage

notes:
  Lever 1
  Lever 2
  Lever 3
  Lever 4
  Lever 5
  Lever 8
  Lever 7
  Lever 6

custom parts:
  NodeMCU V1.0: ESP8266 based NodeMCU
