# Fritzing sketch signal (saved by Fritzing 0.9.3b)

parts:
  U1 = NodeMCU V1.0
  IC1 = Voltage Regulator [package=to220-igo]
  J1 = Basic Servo
  J2 = Basic Servo
  LED1 = smd LED [color="Yellow (595nm)" package="1206 [SMD]"]
  R1 = Resistor [tolerance=±5% resistance=220 package="1206 [SMD]"]
  LED2 = smd LED [color="Yellow (595nm)" package="1206 [SMD]"]
  R2 = Resistor [tolerance=±5% resistance=220 package="1206 [SMD]"]

nets:
  GND: U1.GND, IC1.IN, J1.gnd, J2.gnd, R1.Pin_1, R2.Pin_1
  N1: U1.D5, LED1.anode
  N2: U1.D6, LED2.anode
  VCC: U1.Vin, IC1.OUT, J1.vcc, J2.vcc
  N3: LED1.cathode, R1.Pin_0
  N4: LED2.cathode, R2.Pin_0

notes:
  servo 1
  servo 2
  LED 1
  LED 2

custom parts:
  NodeMCU V1.0: ESP8266 based NodeMCU
